# Fritzing sketch Aquaponik (saved by Fritzing 0.9.3b)
breadboards: 1

parts:
  U1 = NodeMCU V1.0
  Q1 = TRANSISTOR_NPN [package=to-92-ammo]
  YL-1 = YL-38 Humitidy Sensor
  Pumpe = DC Motor

nets:
  3V3: U1.3V3, YL-1.VCC
  GND: U1.GND, YL-1.GND, Pumpe.pin_2
  N1: U1.RSV, Q1.C
  N2: U1.A0, YL-1.ANALOG
  N3: Q1.E, Pumpe.pin_1
  N4: Q1.B, YL-1.DIGITAL

custom parts:
  NodeMCU V1.0: ESP8266 based NodeMCU
